# Fritzing sketch wiring (saved by Fritzing 0.9.2b)

parts:
  Part1 = Arduino Pro Mini v13
  AMP1 = MAX98306_Stereo_Amplifier
  Part2 = femtobuck
  9V_1A_power_supply = 2.1mm DC Barrel Jack
  SP1 = SPEAKER [package=pcb_mount_speaker]
  SP2 = SPEAKER [package=pcb_mount_speaker]
  LED2 = LED - 3mm [color="Red (633nm)" package="3 mm [THT]"]
  SONAR3 = Maxbotix MaxSonar Ultrasonic Sensor
  U1 = Voltage Regulator - 5V [package="DPak [SMD]"]

nets:
  N1: Part1.RAW, Part2.V+, 9V_1A_power_supply.center, U1.input_voltage
  GND: Part1.GND, AMP1.connector2, AMP1.connector5, AMP1.connector6, Part2.V-, Part2.D-, 9V_1A_power_supply.sleeve, SONAR3.GND, U1.GND
  N2: Part1.D13/SCK, SONAR3.RX
  N3: Part1.D12/MISO, SONAR3.TX
  N4: Part1.D11_PWM/MOSI, AMP1.connector4, AMP1.connector7
  N5: Part1.D4, Part2.D+
  N6: AMP1.connector1, SONAR3.+5V, U1.output_voltage
  N7: AMP1.connector10, SP1.+
  N8: AMP1.connector11, SP1.-
  N9: AMP1.connector12, SP2.+
  N10: AMP1.connector13, SP2.-
  N11: Part2.LED-, LED2.cathode
  N12: Part2.LED+, LED2.anode

notes:
  SainSmart HC-SR04

custom parts:
  femtobuck: Description: This is the FemtoBuck, a small-size single-output constant current LED driver. Each FemtoBuck has the capability to dim a single high-power channel of LEDs from 0-350mA at up to 36V while the dimming control can be either accessed via PWM or analog signal from 0-2.5V. This board is based off of the PicoBuck LED Driver, developed in collaboration with Ethan Zonca, except instead of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
  2.1mm DC Barrel Jack: 2.1mm DC Barrel Jack with Thru-Hole Connectors (breadboardable)
  Maxbotix MaxSonar Ultrasonic Sensor: Maxbotix MaxSonar Ultrasonic Sensor LV-EZ0, LV-EZ1, LV-EZ2, LV-EZ3, LV-EZ4
